// Logisim project ym2602.circ as structural Verilog
module PSG (
  input  clk,
  input  reset,
  input  WR,
  input  IORQ,
  input  A7,
  input  A6,
  input  [7:0] data,
  output [3:0] out_8,
  output [3:0] out_9,
  output [3:0] out_10,
  output [3:0] out_11
);

  wire and_1_out, and_6_out, and_7_out, and_8_out, cmp_bit_1_cout, cmp_bit_2_cout, cmp_bit_3_cout,
       cmp_bit_4_cout, cmp_bit_5_cout, cmp_bit_6_cout, cmp_bit_7_cout, cmp_bit_8_cout, cmp_bit_9_cout,
       cmp_bit_10_cout, d_ff_9_q, d_ff_9_qn, d_ff_10_q, d_ff_10_qn, d_ff_11_q, d_ff_11_qn, d_ff_12_q,
       d_ff_13_q, d_ff_14_q, d_ff_15_q, d_ff_16_q, d_ff_17_q, d_ff_18_q, d_ff_19_q, d_ff_20_q, d_ff_21_q,
       d_ff_21_qn, d_ff_22_q, d_ff_23_q, d_ff_24_q, d_ff_25_q, d_ff_26_q, d_ff_27_qn, d_ff_28_q, d_ff_29_q,
       d_ff_30_q, nor_1_out, nor_2_out, nor_3_out, nor_7_out, nor_9_out, nor_10_out, nor_11_out, nor_12_out,
       nor_13_out, nor_14_out, not_1_out, not_2_out, not_3_out, not_4_out, not_5_out, not_6_out, not_7_out,
       not_8_out, not_9_out, not_10_out, not_11_out, not_12_out, not_13_out, not_14_out, not_15_out,
       not_16_out, not_17_out, not_18_out, not_19_out, not_20_out, not_21_out, not_22_out, not_23_out,
       not_24_out, not_25_out, not_26_out, not_27_out, not_28_out, not_29_out, or_1_out, or_2_out, or_3_out,
       or_4_out, or_5_out, or_6_out, or_7_out, or_8_out, or_9_out, or_10_out, or_11_out, or_12_out,
       or_13_out, or_14_out, psg_clk_1_clk1, psg_clk_1_clk2, psg_clk_1_hclk1, psg_clk_1_hclk2,
       psg_clk_1_reset_sync, psg_noise_bit_1_valout, psg_noise_bit_2_valout, psg_noise_bit_3_valout,
       psg_noise_bit_4_valout, psg_noise_bit_5_valout, psg_noise_bit_6_valout, psg_noise_bit_7_valout,
       psg_noise_bit_8_valout, psg_noise_bit_9_valout, psg_noise_bit_10_valout, psg_noise_bit_11_valout,
       psg_noise_bit_12_valout, psg_noise_bit_13_valout, psg_noise_bit_14_valout, psg_noise_bit_15_valout,
       psg_noise_bit_16_valout, psg_reg_bit2_1_out_5, psg_reg_bit2_2_out_5, psg_reg_bit2_3_out_5,
       psg_sign_bit_1_sign, psg_sign_bit_1_valout, psg_sign_bit_2_sign, psg_sign_bit_2_valout,
       psg_sign_bit_3_sign, psg_sign_bit_3_valout, psg_sign_bit_4_sign, xor_1_out;
  wire [3:0] bit_extender_6_out, bit_extender_7_out, bit_extender_8_out, bit_extender_9_out,
       psg_reg_bit3_1_out_5, psg_reg_bit3_5_out_5, psg_reg_bit3_9_out_5, psg_reg_bit3_13_out_5;
  wire [6:4] nor_4_out;
  wire [7:0] d_ff_1_q;
  wire [9:0] adder_1_out, and_2_out, and_3_out, and_4_out, and_5_out, and_9_out, bit_extender_1_out,
       bit_extender_2_out, bit_extender_3_out, bit_extender_4_out, bit_extender_5_out, latch_10bit_1_val_out,
       latch_10bit_2_val_out, latch_10bit_3_val_out, latch_10bit_4_val_out, latch_10bit_5_val_out,
       latch_10bit_6_val_out, latch_10bit_7_val_out, latch_10bit_8_val_out, latch_10bit_9_val_out, nor_8_out,
       psg_reg_bit_1_out_5, psg_reg_bit_11_out_5, psg_reg_bit_21_out_5;

  not not_1 (not_1_out, A6);
  or or_1 (or_1_out, WR, IORQ, A7, not_1_out);
  not not_2 (not_2_out, or_1_out);
  not not_3 (not_3_out, or_2_out);
  not not_4 (not_4_out, or_7_out);
  D_Flip_Flop #(.trigger("high")) d_ff_1 (.D(data[0]), .clk(not_2_out), .Q(d_ff_1_q[0]));  // open: Qn, preset, reset
  D_Flip_Flop #(.trigger("high")) d_ff_2 (.D(data[1]), .clk(not_2_out), .Q(d_ff_1_q[1]));  // open: Qn, preset, reset
  D_Flip_Flop #(.trigger("high")) d_ff_3 (.D(data[2]), .clk(not_2_out), .Q(d_ff_1_q[2]));  // open: Qn, preset, reset
  D_Flip_Flop #(.trigger("high")) d_ff_4 (.D(data[3]), .clk(not_2_out), .Q(d_ff_1_q[3]));  // open: Qn, preset, reset
  D_Flip_Flop #(.trigger("high")) d_ff_5 (.D(data[4]), .clk(not_2_out), .Q(d_ff_1_q[4]));  // open: Qn, preset, reset
  D_Flip_Flop #(.trigger("high")) d_ff_6 (.D(data[5]), .clk(not_2_out), .Q(d_ff_1_q[5]));  // open: Qn, preset, reset
  D_Flip_Flop #(.trigger("high")) d_ff_7 (.D(data[6]), .clk(not_2_out), .Q(d_ff_1_q[6]));  // open: Qn, preset, reset
  D_Flip_Flop #(.trigger("high")) d_ff_8 (.D(data[7]), .clk(not_2_out), .Q(d_ff_1_q[7]));  // open: Qn, preset, reset
  psg_clk psg_clk_1 (
    .clk(clk), .reset(reset), .clk1(psg_clk_1_clk1), .clk2(psg_clk_1_clk2), .hclk1(psg_clk_1_hclk1),
    .hclk2(psg_clk_1_hclk2), .reset_sync(psg_clk_1_reset_sync));
  psg_reg_bit psg_reg_bit_1 (
    .val(d_ff_1_q[0]), .wr(not_3_out), .nwr(or_2_out), .reset(psg_clk_1_reset_sync),
    .out_5(psg_reg_bit_1_out_5[0]));
  psg_reg_bit psg_reg_bit_2 (
    .val(d_ff_1_q[1]), .wr(not_3_out), .nwr(or_2_out), .reset(psg_clk_1_reset_sync),
    .out_5(psg_reg_bit_1_out_5[1]));
  psg_reg_bit psg_reg_bit_3 (
    .val(d_ff_1_q[2]), .wr(not_3_out), .nwr(or_2_out), .reset(psg_clk_1_reset_sync),
    .out_5(psg_reg_bit_1_out_5[2]));
  psg_reg_bit psg_reg_bit_4 (
    .val(d_ff_1_q[3]), .wr(not_3_out), .nwr(or_2_out), .reset(psg_clk_1_reset_sync),
    .out_5(psg_reg_bit_1_out_5[3]));
  psg_reg_bit psg_reg_bit_5 (
    .val(d_ff_1_q[0]), .wr(not_4_out), .nwr(or_7_out), .reset(psg_clk_1_reset_sync),
    .out_5(psg_reg_bit_1_out_5[4]));
  psg_reg_bit psg_reg_bit_6 (
    .val(d_ff_1_q[1]), .wr(not_4_out), .nwr(or_7_out), .reset(psg_clk_1_reset_sync),
    .out_5(psg_reg_bit_1_out_5[5]));
  psg_reg_bit psg_reg_bit_7 (
    .val(d_ff_1_q[2]), .wr(not_4_out), .nwr(or_7_out), .reset(psg_clk_1_reset_sync),
    .out_5(psg_reg_bit_1_out_5[6]));
  psg_reg_bit psg_reg_bit_8 (
    .val(d_ff_1_q[3]), .wr(not_4_out), .nwr(or_7_out), .reset(psg_clk_1_reset_sync),
    .out_5(psg_reg_bit_1_out_5[7]));
  psg_reg_bit psg_reg_bit_9 (
    .val(d_ff_1_q[4]), .wr(not_4_out), .nwr(or_7_out), .reset(psg_clk_1_reset_sync),
    .out_5(psg_reg_bit_1_out_5[8]));
  psg_reg_bit psg_reg_bit_10 (
    .val(d_ff_1_q[5]), .wr(not_4_out), .nwr(or_7_out), .reset(psg_clk_1_reset_sync),
    .out_5(psg_reg_bit_1_out_5[9]));
  nor nor_1 (nor_1_out, not_2_out, nor_2_out);
  nor nor_2 (nor_2_out, nor_1_out, d_ff_13_q);
  and and_1 (and_1_out, d_ff_13_q, d_ff_1_q[7]);
  nor nor_3 (nor_3_out, not_2_out, nor_1_out);
  D_Flip_Flop #(.trigger("high")) d_ff_9 (
    .D(d_ff_1_q[4]), .clk(and_1_out), .Q(d_ff_9_q), .Qn(d_ff_9_qn));  // open: preset, reset
  D_Flip_Flop #(.trigger("high")) d_ff_10 (
    .D(d_ff_1_q[5]), .clk(and_1_out), .Q(d_ff_10_q), .Qn(d_ff_10_qn));  // open: preset, reset
  D_Flip_Flop #(.trigger("high")) d_ff_11 (
    .D(d_ff_1_q[6]), .clk(and_1_out), .Q(d_ff_11_q), .Qn(d_ff_11_qn));  // open: preset, reset
  not not_5 (not_5_out, d_ff_1_q[7]);
  not not_6 (not_6_out, or_3_out);
  not not_7 (not_7_out, or_6_out);
  D_Flip_Flop #(.trigger("high")) d_ff_12 (
    .D(nor_3_out), .clk(psg_clk_1_clk1), .Q(d_ff_12_q));  // open: Qn, preset, reset
  psg_reg_bit psg_reg_bit_11 (
    .val(d_ff_1_q[0]), .wr(not_6_out), .nwr(or_3_out), .reset(psg_clk_1_reset_sync),
    .out_5(psg_reg_bit_11_out_5[0]));
  psg_reg_bit psg_reg_bit_12 (
    .val(d_ff_1_q[1]), .wr(not_6_out), .nwr(or_3_out), .reset(psg_clk_1_reset_sync),
    .out_5(psg_reg_bit_11_out_5[1]));
  psg_reg_bit psg_reg_bit_13 (
    .val(d_ff_1_q[2]), .wr(not_6_out), .nwr(or_3_out), .reset(psg_clk_1_reset_sync),
    .out_5(psg_reg_bit_11_out_5[2]));
  psg_reg_bit psg_reg_bit_14 (
    .val(d_ff_1_q[3]), .wr(not_6_out), .nwr(or_3_out), .reset(psg_clk_1_reset_sync),
    .out_5(psg_reg_bit_11_out_5[3]));
  psg_reg_bit psg_reg_bit_15 (
    .val(d_ff_1_q[0]), .wr(not_7_out), .nwr(or_6_out), .reset(psg_clk_1_reset_sync),
    .out_5(psg_reg_bit_11_out_5[4]));
  psg_reg_bit psg_reg_bit_16 (
    .val(d_ff_1_q[1]), .wr(not_7_out), .nwr(or_6_out), .reset(psg_clk_1_reset_sync),
    .out_5(psg_reg_bit_11_out_5[5]));
  psg_reg_bit psg_reg_bit_17 (
    .val(d_ff_1_q[2]), .wr(not_7_out), .nwr(or_6_out), .reset(psg_clk_1_reset_sync),
    .out_5(psg_reg_bit_11_out_5[6]));
  psg_reg_bit psg_reg_bit_18 (
    .val(d_ff_1_q[3]), .wr(not_7_out), .nwr(or_6_out), .reset(psg_clk_1_reset_sync),
    .out_5(psg_reg_bit_11_out_5[7]));
  psg_reg_bit psg_reg_bit_19 (
    .val(d_ff_1_q[4]), .wr(not_7_out), .nwr(or_6_out), .reset(psg_clk_1_reset_sync),
    .out_5(psg_reg_bit_11_out_5[8]));
  psg_reg_bit psg_reg_bit_20 (
    .val(d_ff_1_q[5]), .wr(not_7_out), .nwr(or_6_out), .reset(psg_clk_1_reset_sync),
    .out_5(psg_reg_bit_11_out_5[9]));
  D_Flip_Flop #(.trigger("high")) d_ff_13 (
    .D(d_ff_12_q), .clk(psg_clk_1_clk2), .Q(d_ff_13_q));  // open: Qn, preset, reset
  or or_2 (or_2_out, d_ff_9_q, d_ff_10_q, d_ff_11_q, not_5_out, d_ff_15_q);
  or or_3 (or_3_out, d_ff_9_q, d_ff_10_qn, d_ff_11_q, not_5_out, d_ff_15_q);
  or or_4 (or_4_out, d_ff_9_q, d_ff_10_q, d_ff_11_qn, d_ff_15_q, not_5_out);
  or or_5 (or_5_out, d_ff_9_q, d_ff_10_q, d_ff_11_qn, d_ff_1_q[7], d_ff_15_q);
  or or_6 (or_6_out, d_ff_9_q, d_ff_10_qn, d_ff_11_q, d_ff_1_q[7], d_ff_15_q);
  or or_7 (or_7_out, d_ff_9_q, d_ff_10_q, d_ff_11_q, d_ff_1_q[7], d_ff_15_q);
  or or_8 (or_8_out, d_ff_9_qn, d_ff_10_q, d_ff_11_q, d_ff_15_q);
  or or_9 (or_9_out, d_ff_9_qn, d_ff_10_qn, d_ff_11_q, d_ff_15_q);
  or or_10 (or_10_out, d_ff_9_qn, d_ff_10_q, d_ff_11_qn, d_ff_15_q);
  or or_11 (or_11_out, d_ff_9_qn, d_ff_10_qn, d_ff_11_qn, d_ff_15_q);
  or or_12 (or_12_out, d_ff_9_q, d_ff_10_qn, d_ff_11_qn, d_ff_15_q);
  D_Flip_Flop #(.trigger("high")) d_ff_14 (
    .D(d_ff_13_q), .clk(psg_clk_1_clk1), .Q(d_ff_14_q));  // open: Qn, preset, reset
  D_Flip_Flop #(.trigger("high")) d_ff_15 (
    .D(d_ff_14_q), .clk(psg_clk_1_clk2), .Q(d_ff_15_q));  // open: Qn, preset, reset
  not not_8 (not_8_out, or_4_out);
  not not_9 (not_9_out, or_5_out);
  not not_10 (not_10_out, or_12_out);
  psg_reg_bit psg_reg_bit_21 (
    .val(d_ff_1_q[0]), .wr(not_8_out), .nwr(or_4_out), .reset(psg_clk_1_reset_sync),
    .out_5(psg_reg_bit_21_out_5[0]));
  psg_reg_bit psg_reg_bit_22 (
    .val(d_ff_1_q[1]), .wr(not_8_out), .nwr(or_4_out), .reset(psg_clk_1_reset_sync),
    .out_5(psg_reg_bit_21_out_5[1]));
  psg_reg_bit psg_reg_bit_23 (
    .val(d_ff_1_q[2]), .wr(not_8_out), .nwr(or_4_out), .reset(psg_clk_1_reset_sync),
    .out_5(psg_reg_bit_21_out_5[2]));
  psg_reg_bit psg_reg_bit_24 (
    .val(d_ff_1_q[3]), .wr(not_8_out), .nwr(or_4_out), .reset(psg_clk_1_reset_sync),
    .out_5(psg_reg_bit_21_out_5[3]));
  psg_reg_bit psg_reg_bit_25 (
    .val(d_ff_1_q[0]), .wr(not_9_out), .nwr(or_5_out), .reset(psg_clk_1_reset_sync),
    .out_5(psg_reg_bit_21_out_5[4]));
  psg_reg_bit psg_reg_bit_26 (
    .val(d_ff_1_q[1]), .wr(not_9_out), .nwr(or_5_out), .reset(psg_clk_1_reset_sync),
    .out_5(psg_reg_bit_21_out_5[5]));
  psg_reg_bit psg_reg_bit_27 (
    .val(d_ff_1_q[2]), .wr(not_9_out), .nwr(or_5_out), .reset(psg_clk_1_reset_sync),
    .out_5(psg_reg_bit_21_out_5[6]));
  psg_reg_bit psg_reg_bit_28 (
    .val(d_ff_1_q[3]), .wr(not_9_out), .nwr(or_5_out), .reset(psg_clk_1_reset_sync),
    .out_5(psg_reg_bit_21_out_5[7]));
  psg_reg_bit psg_reg_bit_29 (
    .val(d_ff_1_q[4]), .wr(not_9_out), .nwr(or_5_out), .reset(psg_clk_1_reset_sync),
    .out_5(psg_reg_bit_21_out_5[8]));
  psg_reg_bit psg_reg_bit_30 (
    .val(d_ff_1_q[5]), .wr(not_9_out), .nwr(or_5_out), .reset(psg_clk_1_reset_sync),
    .out_5(psg_reg_bit_21_out_5[9]));
  not not_11 (not_11_out, psg_reg_bit2_2_out_5);
  not not_12 (not_12_out, psg_reg_bit2_1_out_5);
  nor nor_4 (nor_4_out[4], psg_reg_bit2_2_out_5, psg_reg_bit2_1_out_5);
  nor nor_5 (nor_4_out[5], not_11_out, psg_reg_bit2_1_out_5);
  nor nor_6 (nor_4_out[6], psg_reg_bit2_2_out_5, not_12_out);
  nor nor_7 (nor_7_out, not_11_out, not_12_out);
  assign bit_extender_1_out = {{9{d_ff_24_q}}, d_ff_24_q};  // Bit_Extender bit_extender_1
  assign bit_extender_2_out = {{9{d_ff_23_q}}, d_ff_23_q};  // Bit_Extender bit_extender_2
  assign bit_extender_3_out = {{9{d_ff_22_q}}, d_ff_22_q};  // Bit_Extender bit_extender_3
  assign bit_extender_4_out = {{9{d_ff_25_q}}, d_ff_25_q};  // Bit_Extender bit_extender_4
  psg_reg_bit2 psg_reg_bit2_1 (
    .val(d_ff_1_q[0]), .wr(not_10_out), .nwr(or_12_out), .reset(psg_clk_1_reset_sync),
    .out_5(psg_reg_bit2_1_out_5));
  psg_reg_bit2 psg_reg_bit2_2 (
    .val(d_ff_1_q[1]), .wr(not_10_out), .nwr(or_12_out), .reset(psg_clk_1_reset_sync),
    .out_5(psg_reg_bit2_2_out_5));
  psg_reg_bit2 psg_reg_bit2_3 (
    .val(d_ff_1_q[2]), .wr(not_10_out), .nwr(or_12_out), .reset(psg_clk_1_reset_sync),
    .out_5(psg_reg_bit2_3_out_5));
  assign and_2_out = psg_reg_bit_21_out_5 & bit_extender_1_out;  // AND_Gate and_2, 10 bits wide
  assign and_3_out = psg_reg_bit_11_out_5 & bit_extender_2_out;  // AND_Gate and_3, 10 bits wide
  assign and_4_out = psg_reg_bit_1_out_5 & bit_extender_3_out;  // AND_Gate and_4, 10 bits wide
  assign and_5_out = bit_extender_4_out & {3'b000, nor_4_out, 4'b0000};  // AND_Gate and_5, 10 bits wide
  assign nor_8_out = ~(and_2_out | and_3_out | and_4_out | and_5_out);  // NOR_Gate nor_8, 10 bits wide
  nor nor_9 (nor_9_out, d_ff_22_q, d_ff_23_q, d_ff_24_q, psg_clk_1_reset_sync);
  D_Flip_Flop #(.trigger("high")) d_ff_16 (
    .D(nor_9_out), .clk(psg_clk_1_hclk1), .Q(d_ff_16_q));  // open: Qn, preset, reset
  D_Flip_Flop #(.trigger("high")) d_ff_17 (
    .D(d_ff_22_q), .clk(psg_clk_1_hclk1), .Q(d_ff_17_q));  // open: Qn, preset, reset
  D_Flip_Flop #(.trigger("high")) d_ff_18 (
    .D(d_ff_23_q), .clk(psg_clk_1_hclk1), .Q(d_ff_18_q));  // open: Qn, preset, reset
  D_Flip_Flop #(.trigger("high")) d_ff_19 (
    .D(d_ff_24_q), .clk(psg_clk_1_hclk1), .Q(d_ff_19_q));  // open: Qn, preset, reset
  D_Flip_Flop #(.trigger("high")) d_ff_20 (
    .D(psg_clk_1_reset_sync), .clk(psg_clk_1_hclk1), .Q(d_ff_20_q));  // open: Qn, preset, reset
  D_Flip_Flop #(.trigger("high")) d_ff_21 (
    .D(d_ff_26_q), .clk(psg_clk_1_hclk1), .Q(d_ff_21_q), .Qn(d_ff_21_qn));  // open: preset, reset
  latch_10bit latch_10bit_1 (.val(nor_8_out), .clk(psg_clk_1_hclk1), .val_out(latch_10bit_1_val_out));
  D_Flip_Flop #(.trigger("high")) d_ff_22 (
    .D(d_ff_16_q), .clk(psg_clk_1_hclk2), .Q(d_ff_22_q));  // open: Qn, preset, reset
  D_Flip_Flop #(.trigger("high")) d_ff_23 (
    .D(d_ff_17_q), .clk(psg_clk_1_hclk2), .Q(d_ff_23_q));  // open: Qn, preset, reset
  D_Flip_Flop #(.trigger("high")) d_ff_24 (
    .D(d_ff_18_q), .clk(psg_clk_1_hclk2), .Q(d_ff_24_q));  // open: Qn, preset, reset
  D_Flip_Flop #(.trigger("high")) d_ff_25 (
    .D(d_ff_19_q), .clk(psg_clk_1_hclk2), .Q(d_ff_25_q));  // open: Qn, preset, reset
  D_Flip_Flop #(.trigger("high")) d_ff_26 (
    .D(d_ff_20_q), .clk(psg_clk_1_hclk2), .Q(d_ff_26_q));  // open: Qn, preset, reset
  not not_13 (not_13_out, d_ff_21_qn);
  D_Flip_Flop #(.trigger("high")) d_ff_27 (
    .D(nor_10_out), .clk(psg_clk_1_hclk2), .Qn(d_ff_27_qn));  // open: Q, preset, reset
  nor nor_10 (nor_10_out, d_ff_21_q, cmp_bit_10_cout);
  not not_14 (not_14_out, not_13_out);
  D_Flip_Flop #(.trigger("high")) d_ff_28 (
    .D(d_ff_22_q), .clk(psg_clk_1_hclk1), .Q(d_ff_28_q));  // open: Qn, preset, reset
  not not_15 (not_15_out, psg_sign_bit_1_sign);
  not not_16 (not_16_out, nor_7_out);
  not not_17 (not_17_out, psg_sign_bit_3_sign);
  and and_6 (and_6_out, not_15_out, not_16_out);
  and and_7 (and_7_out, not_17_out, nor_7_out);
  psg_sign_bit psg_sign_bit_1 (
    .step(d_ff_28_q), .reset(not_14_out), .val(cmp_bit_10_cout), .clk1(psg_clk_1_hclk1),
    .clk2(psg_clk_1_hclk2), .sign(psg_sign_bit_1_sign), .valout(psg_sign_bit_1_valout));
  psg_sign_bit psg_sign_bit_2 (
    .step(d_ff_28_q), .reset(not_14_out), .val(psg_sign_bit_3_valout), .clk1(psg_clk_1_hclk1),
    .clk2(psg_clk_1_hclk2), .sign(psg_sign_bit_2_sign), .valout(psg_sign_bit_2_valout));
  nor nor_11 (nor_11_out, and_6_out, and_7_out);
  not not_18 (not_18_out, or_12_out);
  D_Flip_Flop #(.trigger("high")) d_ff_29 (
    .D(nor_11_out), .clk(psg_clk_1_hclk1), .Q(d_ff_29_q));  // open: Qn, preset, reset
  Adder #(.width(10)) adder_1 (.a(latch_10bit_9_val_out), .b({10{1'b0}}), .out(adder_1_out), .cin(1'b1));  // open: cout
  cmp_bit cmp_bit_1 (.cin(1'b1), .a(latch_10bit_1_val_out[0]), .b(latch_10bit_2_val_out[0]), .cout(cmp_bit_1_cout));
  cmp_bit cmp_bit_2 (
    .cin(cmp_bit_1_cout), .a(latch_10bit_1_val_out[1]), .b(latch_10bit_2_val_out[1]), .cout(cmp_bit_2_cout));
  cmp_bit cmp_bit_3 (
    .cin(cmp_bit_2_cout), .a(latch_10bit_1_val_out[2]), .b(latch_10bit_2_val_out[2]), .cout(cmp_bit_3_cout));
  cmp_bit cmp_bit_4 (
    .cin(cmp_bit_3_cout), .a(latch_10bit_1_val_out[3]), .b(latch_10bit_2_val_out[3]), .cout(cmp_bit_4_cout));
  cmp_bit cmp_bit_5 (
    .cin(cmp_bit_4_cout), .a(latch_10bit_1_val_out[4]), .b(latch_10bit_2_val_out[4]), .cout(cmp_bit_5_cout));
  cmp_bit cmp_bit_6 (
    .cin(cmp_bit_5_cout), .a(latch_10bit_1_val_out[5]), .b(latch_10bit_2_val_out[5]), .cout(cmp_bit_6_cout));
  cmp_bit cmp_bit_7 (
    .cin(cmp_bit_6_cout), .a(latch_10bit_1_val_out[6]), .b(latch_10bit_2_val_out[6]), .cout(cmp_bit_7_cout));
  cmp_bit cmp_bit_8 (
    .cin(cmp_bit_7_cout), .a(latch_10bit_1_val_out[7]), .b(latch_10bit_2_val_out[7]), .cout(cmp_bit_8_cout));
  cmp_bit cmp_bit_9 (
    .cin(cmp_bit_8_cout), .a(latch_10bit_1_val_out[8]), .b(latch_10bit_2_val_out[8]), .cout(cmp_bit_9_cout));
  cmp_bit cmp_bit_10 (
    .cin(cmp_bit_9_cout), .a(latch_10bit_1_val_out[9]), .b(latch_10bit_2_val_out[9]), .cout(cmp_bit_10_cout));
  D_Flip_Flop #(.trigger("high")) d_ff_30 (
    .D(d_ff_29_q), .clk(psg_clk_1_hclk2), .Q(d_ff_30_q));  // open: Qn, preset, reset
  and and_8 (and_8_out, xor_1_out, psg_reg_bit2_3_out_5);
  not not_19 (not_19_out, d_ff_27_qn);
  or or_13 (or_13_out, not_18_out, psg_clk_1_reset_sync);
  not not_20 (not_20_out, d_ff_30_q);
  or or_14 (or_14_out, and_8_out, nor_14_out);
  psg_sign_bit psg_sign_bit_3 (
    .step(d_ff_28_q), .reset(not_14_out), .val(psg_sign_bit_1_valout), .clk1(psg_clk_1_hclk1),
    .clk2(psg_clk_1_hclk2), .sign(psg_sign_bit_3_sign), .valout(psg_sign_bit_3_valout));
  psg_sign_bit psg_sign_bit_4 (
    .step(d_ff_28_q), .reset(not_14_out), .val(psg_sign_bit_2_valout), .clk1(psg_clk_1_hclk1),
    .clk2(psg_clk_1_hclk2), .sign(psg_sign_bit_4_sign));  // open: valout
  assign bit_extender_5_out = {{9{not_19_out}}, not_19_out};  // Bit_Extender bit_extender_5
  not not_21 (not_21_out, or_8_out);
  nor nor_12 (nor_12_out, d_ff_30_q, not_25_out);
  nor nor_13 (nor_13_out, not_20_out, not_24_out);
  latch_10bit latch_10bit_2 (.val(adder_1_out), .clk(psg_clk_1_hclk1), .val_out(latch_10bit_2_val_out));
  latch_10bit latch_10bit_3 (.val(and_9_out), .clk(psg_clk_1_hclk1), .val_out(latch_10bit_3_val_out));
  latch_10bit latch_10bit_4 (.val(latch_10bit_7_val_out), .clk(psg_clk_1_hclk1), .val_out(latch_10bit_4_val_out));
  latch_10bit latch_10bit_5 (.val(latch_10bit_8_val_out), .clk(psg_clk_1_hclk1), .val_out(latch_10bit_5_val_out));
  not not_22 (not_22_out, nor_12_out);
  not not_23 (not_23_out, nor_13_out);
  assign bit_extender_6_out = {{3{psg_sign_bit_4_sign}}, psg_sign_bit_4_sign};  // Bit_Extender bit_extender_6
  not not_24 (not_24_out, not_22_out);
  not not_25 (not_25_out, not_23_out);
  assign out_8 = psg_reg_bit3_1_out_5 | bit_extender_6_out;  // OR_Gate or_15, 4 bits wide
  assign and_9_out = latch_10bit_6_val_out & bit_extender_5_out;  // AND_Gate and_9, 10 bits wide
  psg_reg_bit3 psg_reg_bit3_1 (
    .val(d_ff_1_q[0]), .wr(not_21_out), .nwr(or_8_out), .reset(psg_clk_1_reset_sync),
    .out_5(psg_reg_bit3_1_out_5[0]));
  psg_reg_bit3 psg_reg_bit3_2 (
    .val(d_ff_1_q[1]), .wr(not_21_out), .nwr(or_8_out), .reset(psg_clk_1_reset_sync),
    .out_5(psg_reg_bit3_1_out_5[1]));
  psg_reg_bit3 psg_reg_bit3_3 (
    .val(d_ff_1_q[2]), .wr(not_21_out), .nwr(or_8_out), .reset(psg_clk_1_reset_sync),
    .out_5(psg_reg_bit3_1_out_5[2]));
  psg_reg_bit3 psg_reg_bit3_4 (
    .val(d_ff_1_q[3]), .wr(not_21_out), .nwr(or_8_out), .reset(psg_clk_1_reset_sync),
    .out_5(psg_reg_bit3_1_out_5[3]));
  not not_26 (not_26_out, or_9_out);
  latch_10bit latch_10bit_6 (.val(latch_10bit_2_val_out), .clk(psg_clk_1_hclk2), .val_out(latch_10bit_6_val_out));
  latch_10bit latch_10bit_7 (.val(latch_10bit_3_val_out), .clk(psg_clk_1_hclk2), .val_out(latch_10bit_7_val_out));
  latch_10bit latch_10bit_8 (.val(latch_10bit_4_val_out), .clk(psg_clk_1_hclk2), .val_out(latch_10bit_8_val_out));
  latch_10bit latch_10bit_9 (.val(latch_10bit_5_val_out), .clk(psg_clk_1_hclk2), .val_out(latch_10bit_9_val_out));
  assign bit_extender_7_out = {{3{psg_sign_bit_2_sign}}, psg_sign_bit_2_sign};  // Bit_Extender bit_extender_7
  psg_noise_bit psg_noise_bit_1 (
    .val(or_14_out), .clk1(not_25_out), .clk2(not_24_out), .reset(or_13_out), .valout(psg_noise_bit_1_valout));
  psg_noise_bit psg_noise_bit_2 (
    .val(psg_noise_bit_1_valout), .clk1(not_25_out), .clk2(not_24_out), .reset(or_13_out),
    .valout(psg_noise_bit_2_valout));
  psg_noise_bit psg_noise_bit_3 (
    .val(psg_noise_bit_2_valout), .clk1(not_25_out), .clk2(not_24_out), .reset(or_13_out),
    .valout(psg_noise_bit_3_valout));
  psg_noise_bit psg_noise_bit_4 (
    .val(psg_noise_bit_3_valout), .clk1(not_25_out), .clk2(not_24_out), .reset(or_13_out),
    .valout(psg_noise_bit_4_valout));
  psg_noise_bit psg_noise_bit_5 (
    .val(psg_noise_bit_4_valout), .clk1(not_25_out), .clk2(not_24_out), .reset(or_13_out),
    .valout(psg_noise_bit_5_valout));
  psg_noise_bit psg_noise_bit_6 (
    .val(psg_noise_bit_5_valout), .clk1(not_25_out), .clk2(not_24_out), .reset(or_13_out),
    .valout(psg_noise_bit_6_valout));
  psg_noise_bit psg_noise_bit_7 (
    .val(psg_noise_bit_6_valout), .clk1(not_25_out), .clk2(not_24_out), .reset(or_13_out),
    .valout(psg_noise_bit_7_valout));
  assign out_9 = psg_reg_bit3_5_out_5 | bit_extender_7_out;  // OR_Gate or_16, 4 bits wide
  psg_reg_bit3 psg_reg_bit3_5 (
    .val(d_ff_1_q[0]), .wr(not_26_out), .nwr(or_9_out), .reset(psg_clk_1_reset_sync),
    .out_5(psg_reg_bit3_5_out_5[0]));
  psg_reg_bit3 psg_reg_bit3_6 (
    .val(d_ff_1_q[1]), .wr(not_26_out), .nwr(or_9_out), .reset(psg_clk_1_reset_sync),
    .out_5(psg_reg_bit3_5_out_5[1]));
  psg_reg_bit3 psg_reg_bit3_7 (
    .val(d_ff_1_q[2]), .wr(not_26_out), .nwr(or_9_out), .reset(psg_clk_1_reset_sync),
    .out_5(psg_reg_bit3_5_out_5[2]));
  psg_reg_bit3 psg_reg_bit3_8 (
    .val(d_ff_1_q[3]), .wr(not_26_out), .nwr(or_9_out), .reset(psg_clk_1_reset_sync),
    .out_5(psg_reg_bit3_5_out_5[3]));
  not not_27 (not_27_out, or_10_out);
  assign bit_extender_8_out = {{3{psg_sign_bit_3_sign}}, psg_sign_bit_3_sign};  // Bit_Extender bit_extender_8
  psg_noise_bit psg_noise_bit_8 (
    .val(psg_noise_bit_7_valout), .clk1(not_25_out), .clk2(not_24_out), .reset(or_13_out),
    .valout(psg_noise_bit_8_valout));
  psg_noise_bit psg_noise_bit_9 (
    .val(psg_noise_bit_8_valout), .clk1(not_25_out), .clk2(not_24_out), .reset(or_13_out),
    .valout(psg_noise_bit_9_valout));
  psg_noise_bit psg_noise_bit_10 (
    .val(psg_noise_bit_9_valout), .clk1(not_25_out), .clk2(not_24_out), .reset(or_13_out),
    .valout(psg_noise_bit_10_valout));
  psg_noise_bit psg_noise_bit_11 (
    .val(psg_noise_bit_10_valout), .clk1(not_25_out), .clk2(not_24_out), .reset(or_13_out),
    .valout(psg_noise_bit_11_valout));
  psg_noise_bit psg_noise_bit_12 (
    .val(psg_noise_bit_11_valout), .clk1(not_25_out), .clk2(not_24_out), .reset(or_13_out),
    .valout(psg_noise_bit_12_valout));
  psg_noise_bit psg_noise_bit_13 (
    .val(psg_noise_bit_12_valout), .clk1(not_25_out), .clk2(not_24_out), .reset(or_13_out),
    .valout(psg_noise_bit_13_valout));
  psg_noise_bit psg_noise_bit_14 (
    .val(psg_noise_bit_13_valout), .clk1(not_25_out), .clk2(not_24_out), .reset(or_13_out),
    .valout(psg_noise_bit_14_valout));
  psg_noise_bit psg_noise_bit_15 (
    .val(psg_noise_bit_14_valout), .clk1(not_25_out), .clk2(not_24_out), .reset(or_13_out),
    .valout(psg_noise_bit_15_valout));
  psg_noise_bit psg_noise_bit_16 (
    .val(psg_noise_bit_15_valout), .clk1(not_25_out), .clk2(not_24_out), .reset(or_13_out),
    .valout(psg_noise_bit_16_valout));
  psg_reg_bit3 psg_reg_bit3_9 (
    .val(d_ff_1_q[0]), .wr(not_27_out), .nwr(or_10_out), .reset(psg_clk_1_reset_sync),
    .out_5(psg_reg_bit3_9_out_5[0]));
  psg_reg_bit3 psg_reg_bit3_10 (
    .val(d_ff_1_q[1]), .wr(not_27_out), .nwr(or_10_out), .reset(psg_clk_1_reset_sync),
    .out_5(psg_reg_bit3_9_out_5[1]));
  psg_reg_bit3 psg_reg_bit3_11 (
    .val(d_ff_1_q[2]), .wr(not_27_out), .nwr(or_10_out), .reset(psg_clk_1_reset_sync),
    .out_5(psg_reg_bit3_9_out_5[2]));
  psg_reg_bit3 psg_reg_bit3_12 (
    .val(d_ff_1_q[3]), .wr(not_27_out), .nwr(or_10_out), .reset(psg_clk_1_reset_sync),
    .out_5(psg_reg_bit3_9_out_5[3]));
  assign out_10 = psg_reg_bit3_9_out_5 | bit_extender_8_out;  // OR_Gate or_17, 4 bits wide
  not not_28 (not_28_out, or_11_out);
  xor xor_1 (xor_1_out, psg_noise_bit_13_valout, psg_noise_bit_16_valout);
  not not_29 (not_29_out, psg_noise_bit_15_valout);
  nor nor_14 (nor_14_out, psg_noise_bit_1_valout, psg_noise_bit_2_valout, psg_noise_bit_3_valout, psg_noise_bit_4_valout, psg_noise_bit_5_valout, psg_noise_bit_6_valout, psg_noise_bit_7_valout, psg_noise_bit_8_valout, psg_noise_bit_9_valout, psg_noise_bit_10_valout, psg_noise_bit_11_valout, psg_noise_bit_12_valout, psg_noise_bit_13_valout, psg_noise_bit_14_valout, psg_noise_bit_15_valout);
  assign bit_extender_9_out = {{3{not_29_out}}, not_29_out};  // Bit_Extender bit_extender_9
  psg_reg_bit3 psg_reg_bit3_13 (
    .val(d_ff_1_q[0]), .wr(not_28_out), .nwr(or_11_out), .reset(psg_clk_1_reset_sync),
    .out_5(psg_reg_bit3_13_out_5[0]));
  psg_reg_bit3 psg_reg_bit3_14 (
    .val(d_ff_1_q[1]), .wr(not_28_out), .nwr(or_11_out), .reset(psg_clk_1_reset_sync),
    .out_5(psg_reg_bit3_13_out_5[1]));
  psg_reg_bit3 psg_reg_bit3_15 (
    .val(d_ff_1_q[2]), .wr(not_28_out), .nwr(or_11_out), .reset(psg_clk_1_reset_sync),
    .out_5(psg_reg_bit3_13_out_5[2]));
  psg_reg_bit3 psg_reg_bit3_16 (
    .val(d_ff_1_q[3]), .wr(not_28_out), .nwr(or_11_out), .reset(psg_clk_1_reset_sync),
    .out_5(psg_reg_bit3_13_out_5[3]));
  assign out_11 = psg_reg_bit3_13_out_5 | bit_extender_9_out;  // OR_Gate or_18, 4 bits wide
endmodule

module sr_bit (
  input  val,
  input  clk1,
  input  clk2,
  output valout,
  output nvalout
);

  wire d_ff_1_q;

  D_Flip_Flop #(.trigger("high")) d_ff_1 (.D(val), .clk(clk1), .Q(d_ff_1_q));  // open: Qn, preset, reset
  D_Flip_Flop #(.trigger("high")) d_ff_2 (.D(d_ff_1_q), .clk(clk2), .Q(valout), .Qn(nvalout));  // open: preset, reset
endmodule

module psg_clk (
  input  clk,
  input  reset,
  output clk1,
  output clk2,
  output hclk1,
  output hclk2,
  output reset_sync
);

  wire d_ff_1_q, d_ff_3_q, d_ff_4_qn, d_ff_5_q, d_ff_6_q, d_ff_7_qn, d_ff_8_qn, d_ff_9_q, nor_1_out,
       nor_2_out, nor_3_out, not_1_out, not_4_out, not_5_out, not_6_out, not_7_out, or_1_out, or_2_out,
       or_3_out, or_4_out, xnor_1_out;

  not not_1 (not_1_out, clk);
  or or_1 (or_1_out, clk, clk2);
  or or_2 (or_2_out, not_1_out, clk1);
  not not_2 (clk1, or_1_out);
  not not_3 (clk2, or_2_out);
  D_Flip_Flop #(.trigger("high")) d_ff_1 (.D(reset), .clk(clk1), .Q(d_ff_1_q));  // open: Qn, preset, reset
  D_Flip_Flop #(.trigger("high")) d_ff_2 (.D(d_ff_1_q), .clk(clk2), .Qn(reset_sync));  // open: Q, preset, reset
  not not_4 (not_4_out, reset_sync);
  D_Flip_Flop #(.trigger("high")) d_ff_3 (.D(not_4_out), .clk(clk1), .Q(d_ff_3_q));  // open: Qn, preset, reset
  D_Flip_Flop #(.trigger("high")) d_ff_4 (.D(d_ff_3_q), .clk(clk2), .Qn(d_ff_4_qn));  // open: Q, preset, reset
  nor nor_1 (nor_1_out, d_ff_4_qn, not_4_out);
  nor nor_2 (nor_2_out, d_ff_6_q, nor_1_out);
  D_Flip_Flop #(.trigger("high")) d_ff_5 (.D(nor_2_out), .clk(clk1), .Q(d_ff_5_q));  // open: Qn, preset, reset
  D_Flip_Flop #(.trigger("high")) d_ff_6 (.D(d_ff_5_q), .clk(clk2), .Q(d_ff_6_q));  // open: Qn, preset, reset
  not not_5 (not_5_out, d_ff_6_q);
  xnor xnor_1 (xnor_1_out, not_5_out, d_ff_9_q);
  nor nor_3 (nor_3_out, xnor_1_out, nor_1_out);
  D_Flip_Flop #(.trigger("high")) d_ff_7 (.D(nor_3_out), .clk(clk1), .Qn(d_ff_7_qn));  // open: Q, preset, reset
  D_Flip_Flop #(.trigger("high")) d_ff_8 (.D(d_ff_7_qn), .clk(clk2), .Qn(d_ff_8_qn));  // open: Q, preset, reset
  D_Flip_Flop #(.trigger("high")) d_ff_9 (.D(d_ff_7_qn), .clk(clk2), .Q(d_ff_9_q));  // open: Qn, preset, reset
  not not_6 (not_6_out, d_ff_7_qn);
  or or_3 (or_3_out, d_ff_8_qn, not_6_out);
  not not_7 (not_7_out, d_ff_8_qn);
  or or_4 (or_4_out, not_7_out, d_ff_7_qn);
  not not_8 (hclk1, or_3_out);
  not not_9 (hclk2, or_4_out);
endmodule

module nmi_logic (
  input  reset,
  input  nmi_in,
  input  in_3,
  output nmi
);

  wire nand_1_out, nand_2_out, nand_3_out, nand_4_out, nand_6_out, not_1_out;

  not not_1 (not_1_out, nmi_in);
  nand nand_1 (nand_1_out, nand_2_out, reset, not_1_out);
  nand nand_2 (nand_2_out, nand_1_out, in_3, nand_3_out);
  nand nand_3 (nand_3_out, nand_4_out, reset, in_3);
  nand nand_4 (nand_4_out, nand_1_out, nand_3_out);
  nand nand_5 (nmi, nand_3_out, nand_6_out);
  nand nand_6 (nand_6_out, nmi, reset, nand_2_out);
endmodule

module psg_reg_bit (
  input  val,
  input  wr,
  input  nwr,
  input  reset,
  output out_5
);

  wire controlled_buffer_1_out, d_ff_1_qn;

  assign controlled_buffer_1_out = wr ? val : 1'bz;  // Controlled_Buffer controlled_buffer_1
  assign controlled_buffer_1_out = nwr ? out_5 : 1'bz;  // Controlled_Buffer controlled_buffer_2
  D_Flip_Flop #(.trigger("high")) d_ff_1 (
    .D(controlled_buffer_1_out), .clk(1'b1), .Qn(d_ff_1_qn));  // open: Q, preset, reset
  nor nor_1 (out_5, d_ff_1_qn, reset);
endmodule

module latch_10bit (
  input  [9:0] val,
  input  clk,
  output [9:0] val_out
);

  D_Flip_Flop #(.trigger("high")) d_ff_1 (.D(val[0]), .clk(clk), .Qn(val_out[0]));  // open: Q, preset, reset
  D_Flip_Flop #(.trigger("high")) d_ff_2 (.D(val[1]), .clk(clk), .Qn(val_out[1]));  // open: Q, preset, reset
  D_Flip_Flop #(.trigger("high")) d_ff_3 (.D(val[2]), .clk(clk), .Qn(val_out[2]));  // open: Q, preset, reset
  D_Flip_Flop #(.trigger("high")) d_ff_4 (.D(val[3]), .clk(clk), .Qn(val_out[3]));  // open: Q, preset, reset
  D_Flip_Flop #(.trigger("high")) d_ff_5 (.D(val[4]), .clk(clk), .Qn(val_out[4]));  // open: Q, preset, reset
  D_Flip_Flop #(.trigger("high")) d_ff_6 (.D(val[5]), .clk(clk), .Qn(val_out[5]));  // open: Q, preset, reset
  D_Flip_Flop #(.trigger("high")) d_ff_7 (.D(val[6]), .clk(clk), .Qn(val_out[6]));  // open: Q, preset, reset
  D_Flip_Flop #(.trigger("high")) d_ff_8 (.D(val[7]), .clk(clk), .Qn(val_out[7]));  // open: Q, preset, reset
  D_Flip_Flop #(.trigger("high")) d_ff_9 (.D(val[8]), .clk(clk), .Qn(val_out[8]));  // open: Q, preset, reset
  D_Flip_Flop #(.trigger("high")) d_ff_10 (.D(val[9]), .clk(clk), .Qn(val_out[9]));  // open: Q, preset, reset
endmodule

module cmp_bit (
  input  cin,
  input  a,
  input  b,
  output cout
);

  wire and_1_out, nor_1_out, nor_2_out;

  nor nor_1 (nor_1_out, b, a);
  nor nor_2 (nor_2_out, cin, nor_1_out);
  and and_1 (and_1_out, a, b);
  nor nor_3 (cout, nor_2_out, and_1_out);
endmodule

module psg_reg_bit2 (
  input  val,
  input  wr,
  input  nwr,
  input  reset,
  output out_5
);

  wire controlled_buffer_1_out, d_ff_1_qn, nor_1_out;

  assign controlled_buffer_1_out = wr ? val : 1'bz;  // Controlled_Buffer controlled_buffer_1
  assign controlled_buffer_1_out = nwr ? nor_1_out : 1'bz;  // Controlled_Buffer controlled_buffer_2
  D_Flip_Flop #(.trigger("high")) d_ff_1 (
    .D(controlled_buffer_1_out), .clk(1'b1), .Q(out_5), .Qn(d_ff_1_qn));  // open: preset, reset
  nor nor_1 (nor_1_out, d_ff_1_qn, reset);
endmodule

module psg_sign_bit (
  input  step,
  input  reset,
  input  val,
  input  clk1,
  input  clk2,
  output sign,
  output valout
);

  wire d_ff_1_q, d_ff_4_q, nand_1_out, nor_1_out, xnor_1_out;

  D_Flip_Flop #(.trigger("high")) d_ff_1 (.D(val), .clk(clk1), .Q(d_ff_1_q));  // open: Qn, preset, reset
  nand nand_1 (nand_1_out, valout, step);
  D_Flip_Flop #(.trigger("high")) d_ff_2 (.D(d_ff_1_q), .clk(clk2), .Q(valout));  // open: Qn, preset, reset
  xnor xnor_1 (xnor_1_out, d_ff_4_q, nand_1_out);
  D_Flip_Flop #(.trigger("high")) d_ff_3 (.D(nor_1_out), .clk(clk1), .Qn(sign));  // open: Q, preset, reset
  nor nor_1 (nor_1_out, xnor_1_out, reset);
  D_Flip_Flop #(.trigger("high")) d_ff_4 (.D(sign), .clk(clk2), .Q(d_ff_4_q));  // open: Qn, preset, reset
endmodule

module psg_noise_bit (
  input  val,
  input  clk1,
  input  clk2,
  input  reset,
  output valout
);

  wire controlled_buffer_1_out, controlled_buffer_3_out, d_ff_1_qn, d_ff_2_qn, nor_1_out;

  assign controlled_buffer_1_out = clk1 ? val : 1'bz;  // Controlled_Buffer controlled_buffer_1
  assign controlled_buffer_1_out = clk2 ? nor_1_out : 1'bz;  // Controlled_Buffer controlled_buffer_2
  D_Flip_Flop #(.trigger("high")) d_ff_1 (
    .D(controlled_buffer_1_out), .clk(1'b1), .Qn(d_ff_1_qn));  // open: Q, preset, reset
  nor nor_1 (nor_1_out, d_ff_1_qn, reset);
  assign controlled_buffer_3_out = clk1 ? valout : 1'bz;  // Controlled_Buffer controlled_buffer_3
  assign controlled_buffer_3_out = clk2 ? nor_1_out : 1'bz;  // Controlled_Buffer controlled_buffer_4
  D_Flip_Flop #(.trigger("high")) d_ff_2 (
    .D(controlled_buffer_3_out), .clk(1'b1), .Qn(d_ff_2_qn));  // open: Q, preset, reset
  nor nor_2 (valout, d_ff_2_qn, reset);
endmodule

module psg_reg_bit3 (
  input  val,
  input  wr,
  input  nwr,
  input  reset,
  output out_5
);

  wire controlled_buffer_1_out, d_ff_1_q;

  assign controlled_buffer_1_out = wr ? val : 1'bz;  // Controlled_Buffer controlled_buffer_1
  assign controlled_buffer_1_out = nwr ? out_5 : 1'bz;  // Controlled_Buffer controlled_buffer_2
  D_Flip_Flop #(.trigger("high")) d_ff_1 (
    .D(controlled_buffer_1_out), .clk(1'b1), .Q(d_ff_1_q));  // open: Qn, preset, reset
  or or_1 (out_5, d_ff_1_q, reset);
endmodule

module io_ctrl (
  input  RD,
  input  WR,
  input  IORQ,
  input  A0,
  input  A6,
  input  A7,
  output hv_read
);

  wire d_ff_1_q, d_ff_2_qn, nor_1_out, nor_2_out, nor_3_out, nor_5_out, nor_6_out, nor_7_out, not_1_out,
       not_2_out, not_3_out, not_4_out, not_5_out, not_6_out;

  not not_1 (not_1_out, A7);
  not not_2 (not_2_out, A6);
  not not_3 (not_3_out, d_ff_2_qn);
  or or_1 (hv_read, RD, IORQ, not_2_out, A7);
  nor nor_1 (nor_1_out, RD, IORQ, A6, not_1_out);
  nor nor_2 (nor_2_out, WR, IORQ, A6, not_1_out);
  not not_4 (not_4_out, A0);
  nor nor_3 (nor_3_out, not_3_out, not_6_out);
  // NOR_Gate nor_4 has open pins: in0=d_ff_2_qn, in1=not_6_out, out=open
  nor nor_5 (nor_5_out, d_ff_2_qn, not_6_out);
  // OR_Gate or_2 has open pins: in0=nor_3_out, in1=nor_5_out, in2=nor_7_out, in3=nor_6_out, out=open
  nor nor_6 (nor_6_out, not_5_out, not_4_out);
  nor nor_7 (nor_7_out, not_5_out, A0);
  not not_5 (not_5_out, nor_1_out);
  not not_6 (not_6_out, nor_2_out);
  // OR_Gate or_3 has open pins: in0=nor_1_out, in1=nor_2_out, out=open
  D_Flip_Flop #(.trigger("high")) d_ff_1 (.D(A0), .clk(not_5_out), .Q(d_ff_1_q));  // open: Qn, preset, reset
  D_Flip_Flop #(.trigger("high")) d_ff_2 (.D(A0), .clk(not_6_out), .Qn(d_ff_2_qn));  // open: Q, preset, reset
  // NOR_Gate nor_8 has open pins: in0=d_ff_1_q, in1=not_5_out, out=open
endmodule

module clocks (
  input  xin,
  input  reset,
  output clk1,
  output clk2,
  output hclk1,
  output hclk2,
  output zclk,
  output reset_sync
);

  wire controlled_buffer_1_out, d_ff_1_qn, d_ff_2_q, d_ff_3_qn, d_ff_4_qn, d_ff_5_qn, d_ff_6_qn, d_ff_7_q,
       d_ff_8_qn, d_ff_9_q, d_ff_10_q, d_ff_11_q, d_ff_12_q, multiplexer_1_out, nor_1_out, nor_2_out,
       nor_5_out, nor_6_out, nor_7_out, nor_8_out, not_1_out, not_2_out, not_3_out, not_4_out, not_5_out,
       not_6_out, not_7_out, not_8_out, not_9_out, not_11_out, not_12_out, sr_bit_1_valout, sr_bit_2_nvalout,
       sr_bit_3_valout, sr_bit_4_valout, sr_bit_5_valout, sr_bit_6_valout, sr_bit_7_valout;

  not not_1 (not_1_out, xin);
  D_Flip_Flop #(.trigger("high")) d_ff_1 (.D(d_ff_4_qn), .clk(clk1), .Qn(d_ff_1_qn));  // open: Q, preset, reset
  D_Flip_Flop #(.trigger("high")) d_ff_2 (.D(not_6_out), .clk(clk1), .Q(d_ff_2_q));  // open: Qn, preset, reset
  not not_2 (not_2_out, xin);
  not not_3 (not_3_out, not_1_out);
  sr_bit sr_bit_1 (.clk2(clk1), .val(reset), .clk1(clk2), .valout(sr_bit_1_valout));  // open: nvalout
  sr_bit sr_bit_2 (.clk2(clk1), .val(sr_bit_1_valout), .clk1(clk2), .nvalout(sr_bit_2_nvalout));  // open: valout
  not not_4 (not_4_out, not_2_out);
  not not_5 (not_5_out, not_3_out);
  D_Flip_Flop #(.trigger("high")) d_ff_3 (.D(nor_1_out), .clk(clk2), .Qn(d_ff_3_qn));  // open: Q, preset, reset
  nor nor_1 (nor_1_out, d_ff_1_qn, d_ff_2_q);
  nor nor_2 (nor_2_out, sr_bit_2_nvalout, reset);
  nor nor_3 (clk1, not_4_out, clk2);
  nor nor_4 (clk2, not_5_out, clk1);
  D_Flip_Flop #(.trigger("high")) d_ff_4 (.D(nor_2_out), .clk(clk2), .Qn(d_ff_4_qn));  // open: Q, preset, reset
  assign controlled_buffer_1_out = hclk2 ? reset : 1'bz;  // Controlled_Buffer controlled_buffer_1
  assign controlled_buffer_1_out = hclk1 ? d_ff_7_q : 1'bz;  // Controlled_Buffer controlled_buffer_2
  D_Flip_Flop #(.trigger("high")) d_ff_5 (.D(d_ff_3_qn), .clk(clk1), .Qn(d_ff_5_qn));  // open: Q, preset, reset
  D_Flip_Flop #(.trigger("high")) d_ff_6 (.D(not_6_out), .clk(clk1), .Qn(d_ff_6_qn));  // open: Q, preset, reset
  not not_6 (not_6_out, d_ff_3_qn);
  D_Flip_Flop #(.trigger("high")) d_ff_7 (
    .D(controlled_buffer_1_out), .clk(1'b1), .Q(d_ff_7_q));  // open: Qn, preset, reset
  D_Flip_Flop #(.trigger("high")) d_ff_8 (.D(d_ff_4_qn), .clk(clk1), .Qn(d_ff_8_qn));  // open: Q, preset, reset
  D_Flip_Flop #(.trigger("high")) d_ff_9 (
    .D(controlled_buffer_1_out), .clk(hclk1), .Q(d_ff_9_q));  // open: Qn, preset, reset
  D_Flip_Flop #(.trigger("high")) d_ff_10 (.D(d_ff_5_qn), .clk(clk2), .Q(d_ff_10_q));  // open: Qn, preset, reset
  D_Flip_Flop #(.trigger("high")) d_ff_11 (.D(d_ff_6_qn), .clk(clk2), .Q(d_ff_11_q));  // open: Qn, preset, reset
  nor nor_5 (nor_5_out, d_ff_8_qn, sr_bit_3_valout, sr_bit_5_valout);
  not not_7 (not_7_out, sr_bit_3_valout);
  sr_bit sr_bit_3 (.clk2(clk1), .val(nor_5_out), .clk1(clk2), .valout(sr_bit_3_valout));  // open: nvalout
  sr_bit sr_bit_4 (.clk2(hclk1), .val(not_7_out), .clk1(hclk2), .valout(sr_bit_4_valout));  // open: nvalout
  nor nor_6 (nor_6_out, d_ff_10_q, not_12_out);
  nor nor_7 (nor_7_out, d_ff_11_q, not_11_out);
  sr_bit sr_bit_5 (.clk2(clk1), .val(sr_bit_3_valout), .clk1(clk2), .valout(sr_bit_5_valout));  // open: nvalout
  sr_bit sr_bit_6 (.clk2(hclk1), .val(sr_bit_4_valout), .clk1(hclk2), .valout(sr_bit_6_valout));  // open: nvalout
  not not_8 (not_8_out, nor_6_out);
  not not_9 (not_9_out, nor_7_out);
  sr_bit sr_bit_7 (.clk2(clk1), .val(sr_bit_5_valout), .clk1(clk2), .valout(sr_bit_7_valout));  // open: nvalout
  not not_10 (hclk2, not_8_out);
  not not_11 (not_11_out, not_8_out);
  not not_12 (not_12_out, not_9_out);
  not not_13 (hclk1, not_9_out);
  D_Flip_Flop #(.trigger("high")) d_ff_12 (.D(sr_bit_3_valout), .clk(clk2), .Q(d_ff_12_q));  // open: Qn, preset, reset
  Multiplexer multiplexer_1 (.in0(hclk2), .in1(1'b0), .out(multiplexer_1_out), .sel(sr_bit_6_valout));
  D_Flip_Flop #(.trigger("high")) d_ff_13 (
    .D(d_ff_9_q), .clk(multiplexer_1_out), .Qn(reset_sync));  // open: Q, preset, reset
  nor nor_8 (nor_8_out, d_ff_12_q, zclk);
  nor nor_9 (zclk, nor_8_out, sr_bit_7_valout);
endmodule
